// Digital circuit BW8cpu.dig as structural Verilog
module BW8cpu (
  input  step,
  input  crystal,
  input  _555,
  output pass,
  output fail
);

  wire a_dbus_a, a_dbus_l, a_lhs_a, a_rhs_a, ack_addr_a, addr_inc, addr_xfer_a, alu_dbus_a, alu_op, alu_res,
       b_dbus_a, b_dbus_l, b_lhs_a, b_rhs_a, Bus_Controller_musteq_dbus_load, c_dbus_a, c_dbus_l, c_lhs_a,
       c_rhs_a, clk, clk_crystal, comparator_1_eq, Control_Unit_p6, d_dbus_a, d_dbus_l, d_lhs_a, d_rhs_a,
       da_dbus_a, da_dbus_l, dec_sp, dp_addr_a, dp_dbus_a, dp_dbus_l, ext, io_addr_a, ir_dbus_l, isr_xfer_a,
       lsb_dbus_a, mem_dbus_a, mem_dbus_l, msb_dbus_a, nclk, noffset, not_1_out, not_2_out, not_3_out,
       not_4_out, not_5_out, nrst, nRST_out, off_dbus_l, pc_addr_a, pc_inc, pc_xfer_a, pc_xfer_l, pch_dbus_l,
       pcl_dbus_l, reg_a, reg_b, reg_c, reg_d, reg_da, reg_dp, reg_pc, reg_sp, reg_x, reg_y, reset_1_out,
       rst, sp_addr_a, sp_dec, sp_inc, sp_xfer_a, sp_xfer_l, sph_dbus_l, spl_dbus_l, sr_dbus_a, sr_dbus_l,
       t_addr_a, th_dbus_a, th_dbus_l, th_lhs_a, tl_dbus_a, tl_dbus_l, tl_rhs_a, x_addr_a, x_dec, x_inc,
       x_xfer_a, x_xfer_l, xh_dbus_l, xl_dbus_l, y_addr_a, y_dec, y_inc, y_xfer_a, y_xfer_l, yh_dbus_l,
       yl_dbus_l;
  wire [2:0] addr_a, Break_out, clk_mode, count, t_state, xfer_l;
  wire [3:0] dbus_a;
  wire [4:0] dbus_l, flags, xfer_a;
  wire [7:0] dbus, driver_1_out, driver_2_out, lhs, mbus, opcode, reg_off, reg_th, reg_tl, rhs;
  wire [15:0] addr, addr_out;
  wire [17:3] Control_Unit_p20;

  PullDown #(.Bits(8)) pulldown_1 (.out(dbus));
  PullDown #(.Bits(16)) pulldown_2 (.out({lhs, rhs}));
  // Probe on dbus
  // Probe on {lhs, rhs}
  // Probe on reg_a
  // Probe on reg_b
  // Probe on reg_c
  // Probe on reg_d
  // Probe on reg_dp
  // Probe on reg_da
  // Probe on reg_tl
  // Probe on reg_th
  // Probe C_f on flags[4]
  // Probe Z_f on flags[3]
  LED led_1 (.in(clk));
  // Probe on addr
  // Probe on mbus
  // Probe on reg_pc
  // Probe on reg_sp
  // Probe on reg_x
  // Probe on reg_y
  // Probe on addr_out
  // Probe on reg_off
  // Probe on alu_res
  // Probe N_f on flags[1]
  // Probe V_f on flags[2]
  // Probe I_f on flags[0]
  PullDown #(.Bits(16)) pulldown_3 (.out(addr));
  PullDown #(.Bits(8)) pulldown_4 (.out(mbus));
  // Probe on opcode
  // Probe on ext
  Reset reset_1 (.out(reset_1_out));
  Button #(.activeLow("true")) u_nRST (.out(nRST_out));
  Button #(.activeLow("true")) Run (.out(Break_out[0]));
  Button #(.activeLow("true")) Demo (.out(Break_out[1]));
  Button #(.activeLow("true")) Break (.out(Break_out[2]));
  // Probe on flags
  // control_unit Control_Unit: pin names not known; wires that end beside it: 1'b1, opcode, flags, 1'b1, nrst, Control_Unit_p6, 1'b1, clk, dbus_a, dbus_l, alu_op, xfer_a, xfer_l, addr_a, count, dec_sp, nclk, noffset, rst, {Control_Unit_p20[17:16], ext, Control_Unit_p20[14:3], t_state}
  PullDown pulldown_5 (.out(Control_Unit_p6));
  instruction_register Instruction_Register (
    .dbus(dbus), .ndbus_load(ir_dbus_l), .clr(rst), .nclk(nclk), .opcode(opcode));
  memory_bridge Memory_Bridge (.dbus_assert(mem_dbus_a), .dbus_load(mem_dbus_l), .dbus(dbus), .mbus(mbus));
  ROM #(.AddrBits(16), .isProgramMemory("true"), .Bits(8)) ROM (.A(addr_out), .sel(1'b1), .D(mbus));
  and and_1 (nrst, reset_1_out, nRST_out);
  // Probe on t_state
  // triple_clock triple_clock_1: pin names not known; wires that end beside it: Break_out, 1'b1, {nrst, 2'b11}, crystal, _555, step, clk, clk_crystal, clk_mode
  // Probe on nclk
  LED Run_Mode_Active (.in(clk_mode[0]));
  LED Demo_Mode_Active (.in(clk_mode[1]));
  LED Break_Mode_Active (.in(clk_mode[2]));
  // Probe on count
  // Probe on dec_sp
  LED cpu (.in(clk));
  LED u_crystal (.in(clk_crystal));
  // Probe on addr_a
  // Probe on xfer_l
  // Probe on xfer_a
  bus_controller Bus_Controller (
    .dbus_assert(dbus_a), .xfer_load(xfer_l), .addr_assert(addr_a), .clk(clk), .count(count),
    .dec_sp(dec_sp), .nclk(nclk), .dbus_load(dbus_l), .xfer_assert(xfer_a), .ALU_dbus_assert(alu_dbus_a),
    .A_dbus_assert(a_dbus_a), .B_dbus_assert(b_dbus_a), .C_dbus_assert(c_dbus_a), .D_dbus_assert(d_dbus_a),
    .DP_dbus_assert(dp_dbus_a), .DA_dbus_assert(da_dbus_a), .TH_dbus_assert(th_dbus_a),
    .TL_dbus_assert(tl_dbus_a), .SR_dbus_assert(sr_dbus_a), .MEM_dbus_assert(mem_dbus_a),
    .MSB_dbus_assert(msb_dbus_a), .LSB_dbus_assert(lsb_dbus_a), .A_dbus_load(a_dbus_l),
    .B_dbus_load(b_dbus_l), .C_dbus_load(c_dbus_l), .D_dbus_load(d_dbus_l), .DP_dbus_load(dp_dbus_l),
    .DA_dbus_load(da_dbus_l), .TH_dbus_load(th_dbus_l), .TL_dbus_load(tl_dbus_l), .SR_dbus_load(sr_dbus_l),
    .MEM_dbus_load(mem_dbus_l), .IR_dbus_load(ir_dbus_l), .OFF_dbus_load(off_dbus_l),
    .PCH_dbus_load(pch_dbus_l), .PCL_dbus_load(pcl_dbus_l), .SPH_dbus_load(sph_dbus_l),
    .SPL_dbus_load(spl_dbus_l), .XH_dbus_load(xh_dbus_l), .XL_dbus_load(xl_dbus_l), .YH_dbus_load(yh_dbus_l),
    .YL_dbus_load(yl_dbus_l), .PC_xfer_assert(pc_xfer_a), .SP_xfer_assert(sp_xfer_a),
    .X_xfer_assert(x_xfer_a), .Y_xfer_assert(y_xfer_a), .INT_xfer_assert(isr_xfer_a),
    .addr_xfer_assert(addr_xfer_a), .A_lhs_assert(a_lhs_a), .B_lhs_assert(b_lhs_a), .C_lhs_assert(c_lhs_a),
    .D_lhs_assert(d_lhs_a), .TH_lhs_assert(th_lhs_a), .A_rhs_assert(a_rhs_a), .B_rhs_assert(b_rhs_a),
    .C_rhs_assert(c_rhs_a), .D_rhs_assert(d_rhs_a), .TL_rhs_assert(tl_rhs_a), .PC_xfer_load(pc_xfer_l),
    .SP_xfer_load(sp_xfer_l), .X_xfer_load(x_xfer_l), .Y_xfer_load(y_xfer_l), .ACK_addr_assert(ack_addr_a),
    .PC_addr_assert(pc_addr_a), .SP_addr_assert(sp_addr_a), .X_addr_assert(x_addr_a),
    .Y_addr_assert(y_addr_a), .DP_addr_assert(dp_addr_a), .T_addr_assert(t_addr_a),
    .IO_addr_assert(io_addr_a), .PC_inc(pc_inc), .SP_inc(sp_inc), .X_inc(x_inc), .Y_inc(y_inc),
    .ADDR_inc(addr_inc), .X_dec(x_dec), .Y_dec(y_dec), .SP_dec(sp_dec),
    .MUSTEQ_dbus_load(Bus_Controller_musteq_dbus_load));  // open: BR_dbus_assert, BR_dbus_load
  // Probe on alu_op
  // Probe on dbus_l
  // Probe on dbus_a
  not not_1 (not_1_out, Bus_Controller_musteq_dbus_load);
  assign driver_1_out = not_1_out ? dbus : 8'bz;  // Driver driver_1
  assign driver_2_out = not_1_out ? lhs : 8'bz;  // Driver driver_2
  PullDown #(.Bits(8)) pulldown_6 (.out(driver_2_out));
  Comparator #(.Bits(8)) comparator_1 (.a(driver_1_out), .b(driver_2_out), .eq(comparator_1_eq));  // open: gt, lt
  not not_2 (not_2_out, Bus_Controller_musteq_dbus_load);
  PullDown #(.Bits(8)) pulldown_7 (.out(driver_1_out));
  // alu Arithmetic___Logic_Unit_and_Status_Register: pin names not known; wires that end beside it: alu_op, sr_dbus_l, sr_dbus_a, nclk, rst, lhs, rhs, alu_dbus_a, flags, dbus, alu_res
  // gpr_pair A_and_B: pin names not known; wires that end beside it: a_dbus_l, b_dbus_l, a_dbus_a, b_dbus_a, a_lhs_a, b_lhs_a, a_rhs_a, b_rhs_a, dbus, rst, nclk, reg_a, reg_b, {lhs, rhs}
  // gpr_pair C_and_D: pin names not known; wires that end beside it: c_dbus_l, d_dbus_l, c_dbus_a, d_dbus_a, c_lhs_a, d_lhs_a, c_rhs_a, d_rhs_a, dbus, rst, nclk, reg_c, reg_d, {lhs, rhs}
  // gpr_pair DA_and_DP: pin names not known; wires that end beside it: dp_dbus_l, da_dbus_l, dp_dbus_a, da_dbus_a, 1'b1, 1'b1, 1'b1, 1'b1, dbus, rst, nclk, reg_dp, reg_da, {lhs, rhs}
  temp_reg_pair temp_reg_pair_1 (
    .nhi_dbus_load(th_dbus_l), .nlo_dbus_load(tl_dbus_l), .nhi_dbus_assert(th_dbus_a),
    .nlo_dbus_assert(tl_dbus_a), .nhi_lhs_assert(th_lhs_a), .nlo_lhs_assert(1'b1), .nhi_rhs_assert(1'b1),
    .nlo_rhs_assert(tl_rhs_a), .dbus(dbus), .clr(rst), .nclk(nclk), .naddr_assert(t_addr_a), .reg_hi(reg_th),
    .reg_lo(reg_tl), .xfer({lhs, rhs}), .addr(addr));
  not not_3 (not_3_out, comparator_1_eq);
  and and_2 (pass, comparator_1_eq, not_2_out);
  and and_3 (fail, not_2_out, not_3_out);
  not not_4 (not_4_out, addr_inc);
  not not_5 (not_5_out, ack_addr_a);
  // address_register Program_Counter: pin names not known; wires that end beside it: clk, rst, pc_inc, 1'b1, pc_xfer_l, pc_addr_a, pc_xfer_a, pch_dbus_l, pcl_dbus_l, dbus, addr, {lhs, rhs}, reg_pc
  // address_register Stack_Pointer: pin names not known; wires that end beside it: clk, rst, sp_inc, 1'b1, sp_xfer_l, sp_addr_a, sp_xfer_a, sph_dbus_l, spl_dbus_l, dbus, addr, {lhs, rhs}, reg_sp
  // address_register X_Index: pin names not known; wires that end beside it: clk, rst, x_inc, 1'b1, x_xfer_l, x_addr_a, x_xfer_a, xh_dbus_l, xl_dbus_l, dbus, addr, {lhs, rhs}, reg_x
  // address_register Y_Index: pin names not known; wires that end beside it: clk, rst, y_inc, 1'b1, y_xfer_l, y_addr_a, y_xfer_a, yh_dbus_l, yl_dbus_l, dbus, addr, {lhs, rhs}, reg_y
  address_offset Address_Bridge (
    .dbus(dbus), .addr_in(addr), .noffset_en(noffset), .carry_en(not_4_out), .naddr_xfer_assert(addr_xfer_a),
    .nassert_addr(not_5_out), .clr(rst), .noffset_load(off_dbus_l), .nclock(nclk), .addr_out(addr_out),
    .xfer({lhs, rhs}), .q(reg_off));

  // Other names for the same wires on the sheet: clk_cpu = clk; rst_clk_mode[2] = nrst; xfer[15:0] = {lhs, rhs}

  // Notes on the sheet:
  //   crystal: Hz: 5
  //   External Pinout
  //   Buses & Constants
  //   Registers
  //   ROM loads sim_test.bin
endmodule
