// Digital circuit address_register.dig as structural Verilog
module address_register (
  input  [15:0] xfer,
  input  clk,
  input  clr,
  input  xfer_load,
  input  addr_assert,
  input  xfer_assert,
  input  inc,
  input  dec,
  output [15:0] addr
);

  wire Bits_4_7_p2, Bits_4_7_p3, Bits_8_11_p2, Bits_8_11_p3, Bits_12_15_p2, Bits_12_15_p3, Bits_12_15_p11,
       Bits_12_15_p12, q0, q1, q2, q3, q4, q5, q6, q7, q8, q9, q10, q11, q12, q13, q14, q15;

  // _74193 Bits_12_15: pin names not known; wires that end beside it: xfer[12], Bits_12_15_p2, Bits_12_15_p3, xfer[13], xfer[14], xfer[15], clr, xfer_load, 1'b1, 1'b0, Bits_12_15_p11, Bits_12_15_p12, q12, q13, q14, q15
  // _74574 _74574_1: pin names not known; wires that end beside it: xfer_assert, clk, q8, q9, q10, q11, q12, q13, q14, q15, 1'b1, 1'b0, xfer[8], xfer[9], xfer[10], xfer[11], xfer[12], xfer[13], xfer[14], xfer[15]
  // NotConnected on Bits_12_15_p11
  // NotConnected on Bits_12_15_p12
  // _74193 Bits_8_11: pin names not known; wires that end beside it: xfer[8], Bits_8_11_p2, Bits_8_11_p3, xfer[9], xfer[10], xfer[11], clr, xfer_load, 1'b1, 1'b0, Bits_12_15_p2, Bits_12_15_p3, q8, q9, q10, q11
  // _74574 _74574_2: pin names not known; wires that end beside it: xfer_assert, clk, q0, q1, q2, q3, q4, q5, q6, q7, 1'b1, 1'b0, xfer[0], xfer[1], xfer[2], xfer[3], xfer[4], xfer[5], xfer[6], xfer[7]
  // _74574 _74574_3: pin names not known; wires that end beside it: addr_assert, clk, q8, q9, q10, q11, q12, q13, q14, q15, 1'b1, 1'b0, addr[8], addr[9], addr[10], addr[11], addr[12], addr[13], addr[14], addr[15]
  // _74193 Bits_4_7: pin names not known; wires that end beside it: xfer[4], Bits_4_7_p2, Bits_4_7_p3, xfer[5], xfer[6], xfer[7], clr, xfer_load, 1'b1, 1'b0, Bits_8_11_p2, Bits_8_11_p3, q4, q5, q6, q7
  // _74574 _74574_4: pin names not known; wires that end beside it: addr_assert, clk, q0, q1, q2, q3, q4, q5, q6, q7, 1'b1, 1'b0, addr[0], addr[1], addr[2], addr[3], addr[4], addr[5], addr[6], addr[7]
  // _74193 Bits_0_3: pin names not known; wires that end beside it: xfer[0], dec, inc, xfer[1], xfer[2], xfer[3], clr, xfer_load, 1'b1, 1'b0, Bits_4_7_p2, Bits_4_7_p3, q0, q1, q2, q3, clr, xfer_load
endmodule
