// Digital circuit bus_controller.dig as structural Verilog
module bus_controller (
  input  [3:0] dbus_assert,
  input  [3:0] dbus_load,
  input  [4:0] xfer_assert,
  input  [2:0] xfer_load,
  input  [2:0] addr_assert,
  input  nclk,
  input  [2:0] counter_inc,
  output ALU_dbus_assert,
  output A_dbus_assert,
  output B_dbus_assert,
  output C_dbus_assert,
  output D_dbus_assert,
  output SR_dbus_assert,
  output DP_dbus_assert,
  output T1_dbus_assert,
  output T2_dbus_assert,
  output MEM_dbus_load,
  output A_dbus_load,
  output B_dbus_load,
  output C_dbus_load,
  output D_dbus_load,
  output SR_dbus_load,
  output DP_dbus_load,
  output T1_dbus_load,
  output T2_dbus_load,
  output A_lhs_assert,
  output B_lhs_assert,
  output C_lhs_assert,
  output D_lhs_assert,
  output A_rhs_assert,
  output B_rhs_assert,
  output C_rhs_assert,
  output D_rhs_assert,
  output PC_xfer_assert,
  output SP_xfer_assert,
  output X_xfer_assert,
  output Y_xfer_assert,
  output ISR_xfer_assert,
  output RST_xfer_assert,
  output PC_xfer_load,
  output SP_xfer_load,
  output X_xfer_load,
  output Y_xfer_load,
  output E_xfer_load,
  output PC_addr_assert,
  output SP_addr_assert,
  output X_addr_assert,
  output Y_addr_assert,
  output E_addr_assert,
  output DP_addr_assert,
  output MEM_dbus_assert,
  output IR_dbus_load,
  output T1_rhs_assert,
  output T2_rhs_assert,
  output PC_inc,
  output SP_inc,
  output X_inc,
  output Y_inc,
  output SP_dec,
  output X_dec,
  output Y_dec,
  output DPI_dbus_assert,
  output SPI_xfer_assert
);

  wire _7404_1_p2, _7404_1_p3, _7404_1_p4, _7404_1_p5, _7404_1_p6, _7404_1_p9, _7411_2_p3, _7411_2_p4,
       _7411_2_p5, _7411_2_p6, _7411_2_p8, _7411_2_p9, _7421_2_p11, _7421_2_p12, addr_a6, addr_a7, dbus_a13,
       dbus_a14, dbus_a15, dbus_l0, dbus_l11, dbus_l12, dbus_l13, dbus_l14, dbus_l15, select_lhs_assert_p11,
       select_lhs_assert_p12, xfer_a0, xfer_a1, xfer_a2, xfer_a3, xfer_a4, xfer_a5, xfer_a6, xfer_a7,
       xfer_a8, xfer_a9, xfer_a10, xfer_a11, xfer_a12, xfer_a13, xfer_a14, xfer_a15, xfer_a16, xfer_a17,
       xfer_a18, xfer_a19, xfer_a20, xfer_a21, xfer_a22, xfer_a23, xfer_a26, xfer_a27, xfer_a28, xfer_a29,
       xfer_a30, xfer_a31, xfer_l0, xfer_l6, xfer_l7;

  // _74138 DBUS_assert: pin names not known; wires that end beside it: dbus_assert[0], dbus_assert[2], dbus_assert[1], 1'b1, 1'b0, dbus_assert[3], 1'b1, 1'b0, ALU_dbus_assert, A_dbus_assert, B_dbus_assert, C_dbus_assert, D_dbus_assert, SR_dbus_assert, DP_dbus_assert, T1_dbus_assert
  // _74138 _74138_1: pin names not known; wires that end beside it: dbus_assert[0], dbus_assert[2], dbus_assert[1], dbus_assert[3], 1'b0, 1'b0, 1'b1, 1'b0, T2_dbus_assert, MEM_dbus_assert, DPI_dbus_assert, dbus_a13, dbus_a14, dbus_a15
  // _74138 DBUS_load: pin names not known; wires that end beside it: dbus_assert[0], dbus_assert[2], dbus_assert[1], 1'b1, nclk, dbus_load[3], 1'b1, 1'b0, dbus_l0, A_dbus_load, B_dbus_load, C_dbus_load, D_dbus_load, SR_dbus_load, DP_dbus_load, T1_dbus_load
  // _74138 _74138_2: pin names not known; wires that end beside it: dbus_load[0], dbus_load[2], dbus_load[1], dbus_load[3], nclk, 1'b0, 1'b1, 1'b0, T2_dbus_load, MEM_dbus_load, IR_dbus_load, dbus_l11, dbus_l12, dbus_l13, dbus_l14, dbus_l15
  // _7404 _7404_1: pin names not known; wires that end beside it: xfer_assert[4], _7404_1_p2, _7404_1_p3, _7404_1_p4, _7404_1_p5, _7404_1_p6, 1'b1, 1'b0, _7404_1_p9, _7404_1_p9, 1'b0, xfer_a20, xfer_a21, xfer_a22, xfer_a23, ISR_xfer_assert, SPI_xfer_assert, xfer_a26, xfer_a27, xfer_a28, xfer_a29, xfer_a30, xfer_a31
  // NotConnected on _7404_1_p2
  // NotConnected on _7404_1_p3
  // NotConnected on _7404_1_p4
  // NotConnected on _7404_1_p5
  // NotConnected on _7404_1_p6
  // _74154 XFER_assert: pin names not known; wires that end beside it: xfer_assert[0], xfer_assert[2], xfer_assert[1], xfer_assert[3], 1'b0, xfer_assert[4], 1'b1, 1'b0, xfer_assert[2], xfer_assert[3], xfer_a0, xfer_a1, xfer_a2, xfer_a3, xfer_a4, xfer_a5, xfer_a6, xfer_a7, xfer_a8, xfer_a9, xfer_a10, xfer_a11, xfer_a12, xfer_a13, xfer_a14, xfer_a15, xfer_a16, xfer_a17, xfer_a18, xfer_a19
  _74154 _74154_1 (
    .pin1(xfer_assert[0]), .pin2(xfer_assert[1]), .pin3(1'b0), .pin4(1'b1), .pin17(xfer_a30),
    .pin18(xfer_a28), .pin19(xfer_a26), .pin20(ISR_xfer_assert), .pin21(xfer_a22), .pin22(xfer_a20),
    .pin23(xfer_a18), .pin24(xfer_a16));  // open: pin5, pin6, pin7, pin8, pin9, pin10, pin11, pin12, pin13, pin14, pin15, pin16
  // _74138 XFER_load: pin names not known; wires that end beside it: xfer_load[0], xfer_load[2], xfer_load[1], 1'b1, nclk, 1'b0, 1'b1, 1'b0, xfer_l0, PC_xfer_load, SP_xfer_load, X_xfer_load, Y_xfer_load, E_xfer_load, xfer_l6, xfer_l7
  // _74138 ADDR_assert: pin names not known; wires that end beside it: addr_assert[0], addr_assert[2], addr_assert[1], 1'b1, 1'b0, 1'b0, 1'b1, 1'b0, PC_addr_assert, SP_addr_assert, X_addr_assert, Y_addr_assert, E_addr_assert, DP_addr_assert, addr_a6, addr_a7
  // _74138 Counter_Inc_Dec: pin names not known; wires that end beside it: counter_inc[0], counter_inc[2], counter_inc[1], 1'b1, 1'b0, nclk, 1'b1, 1'b0, PC_inc, SP_inc, X_inc, Y_inc, SP_dec, X_dec, Y_dec
  // _7421 select_rhs_assert: pin names not known; wires that end beside it: xfer_a0, xfer_a12, xfer_a1, xfer_a13, xfer_a6, xfer_a7, xfer_a18, xfer_a19, 1'b1, 1'b0, A_rhs_assert, B_rhs_assert
  // _7421 _7421_1: pin names not known; wires that end beside it: xfer_a2, xfer_a14, xfer_a3, xfer_a15, xfer_a8, xfer_a9, xfer_a20, xfer_a21, 1'b1, 1'b0, C_rhs_assert, D_rhs_assert
  // _7421 select_lhs_assert: pin names not known; wires that end beside it: xfer_a0, xfer_a2, xfer_a6, xfer_a8, xfer_a1, xfer_a7, xfer_a3, xfer_a9, 1'b1, 1'b0, select_lhs_assert_p11, select_lhs_assert_p12
  // _7421 _7421_2: pin names not known; wires that end beside it: xfer_a12, xfer_a14, xfer_a18, xfer_a20, xfer_a13, xfer_a19, xfer_a15, xfer_a21, 1'b1, 1'b0, _7421_2_p11, _7421_2_p12
  // _7411 _7411_1: pin names not known; wires that end beside it: select_lhs_assert_p11, xfer_a5, select_lhs_assert_p12, xfer_a11, xfer_a17, _7421_2_p11, xfer_a4, xfer_a10, xfer_a16, 1'b1, 1'b0, A_lhs_assert, B_lhs_assert, C_lhs_assert
  // _7411 _7411_2: pin names not known; wires that end beside it: _7421_2_p12, xfer_a23, _7411_2_p3, _7411_2_p4, _7411_2_p5, _7411_2_p6, xfer_a22, _7411_2_p8, _7411_2_p9, 1'b1, 1'b0, D_lhs_assert
  // NotConnected on _7411_2_p3
  // NotConnected on _7411_2_p4
  // NotConnected on _7411_2_p5
  // NotConnected on _7411_2_p6
  // NotConnected on _7411_2_p8
  // NotConnected on _7411_2_p9
  // _7421 _7421_3: pin names not known; wires that end beside it: xfer_a4, xfer_a16, xfer_a5, xfer_a17, xfer_a10, xfer_a11, xfer_a22, xfer_a23, 1'b1, 1'b0, T1_rhs_assert, T2_rhs_assert

  assign PC_xfer_assert = ISR_xfer_assert;
  assign RST_xfer_assert = ISR_xfer_assert;
  assign SP_xfer_assert = ISR_xfer_assert;
  assign X_xfer_assert = ISR_xfer_assert;
  assign Y_xfer_assert = ISR_xfer_assert;

  // Other names for the same wires on the sheet: addr_a0 = PC_addr_assert; addr_a1 = SP_addr_assert;
  //   addr_a2 = X_addr_assert; addr_a3 = Y_addr_assert; addr_a4 = E_addr_assert; addr_a5 = DP_addr_assert;
  //   aa0 = addr_assert[0]; aa1 = addr_assert[1]; aa2 = addr_assert[2]; count_1 = PC_inc; count_2 = SP_inc;
  //   count_3 = X_inc; count_4 = Y_inc; count_5 = SP_dec; count_6 = X_dec; count_7 = Y_dec; ci0 = counter_inc[0];
  //   ci1 = counter_inc[1]; ci2 = counter_inc[2]; dbus_a0 = ALU_dbus_assert; dbus_a1 = A_dbus_assert;
  //   dbus_a2 = B_dbus_assert; dbus_a3 = C_dbus_assert; dbus_a4 = D_dbus_assert; dbus_a5 = SR_dbus_assert;
  //   dbus_a6 = DP_dbus_assert; dbus_a7 = T1_dbus_assert; dbus_a8 = T2_dbus_assert; dbus_a9 = MEM_dbus_assert;
  //   dbus_a10 = DPI_dbus_assert; da0 = dbus_assert[0]; da1 = dbus_assert[1]; da2 = dbus_assert[2];
  //   da3 = dbus_assert[3]; dbus_l1 = A_dbus_load; dbus_l2 = B_dbus_load; dbus_l3 = C_dbus_load;
  //   dbus_l4 = D_dbus_load; dbus_l5 = SR_dbus_load; dbus_l6 = DP_dbus_load; dbus_l7 = T1_dbus_load;
  //   dbus_l8 = T2_dbus_load; dbus_l9 = MEM_dbus_load; dbus_l10 = IR_dbus_load; dl0 = dbus_load[0];
  //   dl1 = dbus_load[1]; dl2 = dbus_load[2]; dl3 = dbus_load[3]; xfer_a24 = ISR_xfer_assert;
  //   xfer_a25 = SPI_xfer_assert; xa0 = xfer_assert[0]; xa1 = xfer_assert[1]; xa2 = xfer_assert[2];
  //   xa3 = xfer_assert[3]; xa4 = xfer_assert[4]; xfer_l1 = PC_xfer_load; xfer_l2 = SP_xfer_load;
  //   xfer_l3 = X_xfer_load; xfer_l4 = Y_xfer_load; xfer_l5 = E_xfer_load; xl0 = xfer_load[0]; xl1 = xfer_load[1];
  //   xl2 = xfer_load[2]
endmodule
