// Digital circuit instruction_register.dig as structural Verilog
module instruction_register (
  input  [7:0] dbus,
  input  ndbus_load,
  input  nclr,
  output [7:0] opcode
);

  _74ls273 _74ls273_1 (.CP(ndbus_load), .nMR(nclr), .D(dbus), .VCC(1'b1), .GND(1'b0), .Q(opcode));

  // Other names for the same wires on the sheet: q[7:0] = opcode
endmodule
